# Fritzing sketch Wiring_Layout (saved by Fritzing 0.9.5d)
perfboards: 1
breadboards: 1

parts:
  Part1 = Arduino Mega ADK (Rev3)
  Part2 = Adafruit_BMP280
  J1 = Camdenboss CTB0158-6 [part_number=CTB0158-6 package=THT]
  J2 = Camdenboss CTB0158-6 [part_number=CTB0158-6 package=THT]
  BAT1 = Battery Holders [package=lipo-1100mAh]
  LED1 = smd LED [color="Red (633nm)" package="0603 [SMD]"]
  M1 = Stepper Motor - Bipolar
  Part3 = Adafruit MicroSD card breakout board [part_number="Adafruit #254"]
  LED3 = RGB LED (com. cathode, rbg) [package="5 mm [THT]"]
  LED4 = RGB LED (com. cathode, rbg) [package="5 mm [THT]"]
  R8 = Resistor [tolerance=±5% resistance=220 package=THT]
  R9 = Resistor [tolerance=±5% resistance=220 package=THT]
  R10 = Resistor [tolerance=±5% resistance=220 package=THT]
  R11 = Resistor [tolerance=±5% resistance=220 package=THT]
  R12 = Resistor [tolerance=±5% resistance=220 package=THT]
  R13 = Resistor [tolerance=±5% resistance=220 package=THT]
  R14 = Resistor [tolerance=±5% resistance=220 package=THT]
  R16 = Resistor [tolerance=±5% resistance=220 package=THT]
  S2 = Pushbutton [package="[THT]"]

nets:
  N1: Part1.A0, S2.Pin_1, S2.Pin_2
  N2: Part1.A1, R14.Pin_1
  N3: Part1.A2, R12.Pin_1
  N4: Part1.A3, R13.Pin_1
  N5: Part1.A4, R10.Pin_1
  N6: Part1.A5, R8.Pin_1
  N7: Part1.A6, R9.Pin_1
  N8: Part1.D21/SCL, Part2.SCK/SCL
  N9: Part1.D20/SDA, Part2.SDI/SDA
  N10: Part1.D13_PWM, R11.Pin_1
  5V: Part1.5V, Part2.VIN, J2.terminal_2, J2.terminal_4, J2.terminal_6
  GND: Part1.GND, Part2.GND, LED1.cathode, Part3.GND, LED3.common_cathode, LED4.common_cathode, R16.Pin_1
  N11: Part1.D5_PWM, J2.terminal_1
  N12: Part1.D6_PWM, J2.terminal_3
  N13: Part1.D7_PWM, J2.terminal_5
  N14: Part1.D50/MISO, Part3.DO
  N15: Part1.D51/MOSI, Part3.DI
  N16: Part1.D52/SCK, Part3.CLK
  N17: Part1.D53/SS, Part3.CS
  N18: J1.terminal_1, M1.D
  N19: J1.terminal_2, M1.B
  N20: J1.terminal_3, M1.C
  N21: J1.terminal_4, M1.A
  N22: J1.terminal_5, BAT1.-
  N23: J1.terminal_6, BAT1.+
  N24: LED1.anode, R11.Pin_0
  N25: Part3.VCC, R16.Pin_0, S2.Pin_3, S2.Pin_4
  N26: LED3.red_anode, R14.Pin_0
  N27: LED3.blue_anode, R13.Pin_0
  N28: LED3.green_anode, R12.Pin_0
  N29: LED4.red_anode, R10.Pin_0
  N30: LED4.blue_anode, R9.Pin_0
  N31: LED4.green_anode, R8.Pin_0

notes:
  EN-
  EN+
  DIR-
  DIR+
  PUL-
  PUL+
  B-
  GND
  B+
  A-
  A+
  VCC
  Stepper Motor Controller
  [Accell/Gyro] Chip Select (CS)
  MOSO / DO
  CLK
  MOSI / DI
  SPI Connections
  [Wireless] Chip Select (CS)
  Serial Connections
  Gnd
  RX1 (GPS)
  TX1 (GPS)
  ESC Control
  PWM Control

custom parts:
  Adafruit_BMP280: Bosch has stepped up their game with their new BMP280 sensor, an environmental sensor with temperature, barometric pressure that is the next generation upgrade to the BMP085/BMP180/BMP183. This sensor is great for all sorts of weather sensing and can even be used in both I2C and SPI! This precision sensor from Bosch is the best low-cost, precision sensing solution for measuring barometric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
  Adafruit MicroSD card breakout board: Not just a simple breakout board, this microSD adapter goes the extra mile - designed for ease of use. Onboard 5v->3v regulator provides 150mA for power-hungry cards 3v level shifting means you can use this with ease on either 3v or 5v systems Uses a proper level shifting chip, not resistors: less problems, and faster read/write access Use 3 or 4 digital pins to read and write 2Gb+ of storage!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
